// Logisim project Logisim of vehical controling system .circ as structural Verilog: 1 circuit, main circuit main
module main (
  input  in_1,
  output out_2,
  output out_3,
  output out_4,
  output out_5
);

  wire and_1_out, and_2_out, and_3_out, buffer_1_out, buffer_2_out, button_1_out, button_2_out, button_3_out,
       button_4_out, clock_1_out, d_ff_1_q, d_ff_3_qn, d_ff_4_qn, d_ff_5_qn, d_ff_6_qn, d_ff_7_qn, not_1_out;

  Clock clock_1 (.out(clock_1_out));
  Button button_1 (.out(button_1_out));
  Button button_2 (.out(button_2_out));
  Button button_3 (.out(button_3_out));
  Button button_4 (.out(button_4_out));
  D_Flip_Flop d_ff_1 (.clk(d_ff_4_qn), .D(d_ff_4_qn), .Q(d_ff_1_q), .reset(in_1));  // open: Qn, preset, en
  and and_1 (and_1_out, d_ff_1_q, d_ff_3_qn);
  D_Flip_Flop d_ff_2 (.clk(clock_1_out), .D(clock_1_out), .Q(out_3), .reset(and_1_out));  // open: Qn, preset, en
  buf buffer_1 (buffer_1_out, button_2_out);
  buf buffer_2 (buffer_2_out, button_1_out);
  D_Flip_Flop d_ff_3 (.clk(out_3), .D(out_3), .Qn(d_ff_3_qn), .reset(d_ff_3_qn));  // open: Q, preset, en
  D_Flip_Flop d_ff_4 (
    .clk(buffer_1_out), .D(buffer_1_out), .Q(out_2), .Qn(d_ff_4_qn), .reset(out_3));  // open: preset, en
  D_Flip_Flop d_ff_5 (
    .clk(buffer_2_out), .D(buffer_2_out), .Q(out_3), .Qn(d_ff_5_qn), .reset(out_3));  // open: preset, en
  D_Flip_Flop d_ff_6 (
    .clk(button_3_out), .D(button_3_out), .Q(out_4), .Qn(d_ff_6_qn), .reset(out_3));  // open: preset, en
  D_Flip_Flop d_ff_7 (
    .clk(button_4_out), .D(button_4_out), .Q(out_5), .Qn(d_ff_7_qn), .reset(out_3));  // open: preset, en
  and and_2 (and_2_out, d_ff_4_qn, d_ff_5_qn, d_ff_6_qn, d_ff_7_qn);
  LED led_1 (.in(and_2_out));
  not not_1 (not_1_out, and_2_out);
  LED led_2 (.in(not_1_out));
  and and_3 (and_3_out, out_2, out_3, out_4, out_5);
  LED led_3 (.in(and_3_out));
endmodule
