// Logisim project Final logism Alc.circ as structural Verilog: 1 circuit, main circuit main
module main (
  input  in_1,
  input  in_2,
  input  in_3,
  output out_4,
  output out_5,
  output out_6,
  output out_7,
  output out_8,
  output out_9,
  output out_10
);

  wire _1_out, _2_out, _5_out, _9_out, and_1_out, and_2_out, and_3_out, and_4_out, and_5_out, buffer_1_out,
       buffer_2_out, clock_1_out, d_ff_1_q, d_ff_2_q, d_ff_3_qn, d_ff_4_qn, d_ff_5_qn, d_ff_6_qn, d_ff_7_qn,
       not_1_out, S_out;

  Clock clock_1 (.out(clock_1_out));
  Button S (.out(S_out));
  Button _1 (.out(_1_out));
  Button _4 ();  // open: out
  Button _7 ();  // open: out
  D_Flip_Flop d_ff_1 (.clk(d_ff_4_qn), .D(d_ff_4_qn), .Q(d_ff_1_q), .reset(in_1));  // open: Qn, preset, en
  Button _2 (.out(_2_out));
  Button _3 ();  // open: out
  Button _5 (.out(_5_out));
  Button _6 ();  // open: out
  Button _8 ();  // open: out
  Button _9 (.out(_9_out));
  and and_1 (and_1_out, d_ff_1_q, d_ff_3_qn);
  and and_2 (and_2_out, S_out, in_2);
  D_Flip_Flop d_ff_2 (.clk(clock_1_out), .D(clock_1_out), .Q(d_ff_2_q), .reset(and_1_out));  // open: Qn, preset, en
  or or_1 (out_9, and_2_out, in_3);
  buf buffer_1 (buffer_1_out, _5_out);
  buf buffer_2 (buffer_2_out, _2_out);
  D_Flip_Flop d_ff_3 (.clk(d_ff_2_q), .D(d_ff_2_q), .Qn(d_ff_3_qn), .reset(d_ff_3_qn));  // open: Q, preset, en
  D_Flip_Flop d_ff_4 (
    .clk(buffer_1_out), .D(buffer_1_out), .Q(out_4), .Qn(d_ff_4_qn), .reset(d_ff_2_q));  // open: preset, en
  D_Flip_Flop d_ff_5 (
    .clk(buffer_2_out), .D(buffer_2_out), .Q(out_5), .Qn(d_ff_5_qn), .reset(d_ff_2_q));  // open: preset, en
  D_Flip_Flop d_ff_6 (.clk(_1_out), .D(_1_out), .Q(out_6), .Qn(d_ff_6_qn), .reset(d_ff_2_q));  // open: preset, en
  D_Flip_Flop d_ff_7 (.clk(_9_out), .D(_9_out), .Q(out_7), .Qn(d_ff_7_qn), .reset(d_ff_2_q));  // open: preset, en
  and and_3 (and_3_out, d_ff_4_qn, d_ff_5_qn, d_ff_6_qn, d_ff_7_qn);
  LED led_1 (.in(and_3_out));
  and and_4 (and_4_out, out_4, out_5, out_6, out_7);
  and and_5 (and_5_out, and_4_out, out_9);
  LED led_2 (.in(and_4_out));
  LED led_3 (.in(and_5_out));
  not not_1 (not_1_out, and_5_out);
  and and_6 (out_8, and_4_out, not_1_out);

  assign out_10 = out_9;

  // Notes on the sheet:
  //   clock
  //        reset option
  //                       alcohol level
  //   password is wtong
  //   Password is right
  //       detects alcohol
  //   The first is to  enter the password and second is to detect alcohol.
  //   If both are right led is off, else it blinks
  //   Allows driver to drive
endmodule
