// Logisim project alc_logism.circ as structural Verilog: 1 circuit, main circuit main
module main (
  input  in_1,
  input  in_2,
  output out_3,
  output out_4
);

  wire and_1_out, button_1_out;

  Button button_1 (.out(button_1_out));
  and and_1 (and_1_out, button_1_out, in_1);
  or or_1 (out_3, and_1_out, in_2);

  assign out_4 = out_3;

  // Notes on the sheet:
  //   A
  //   B
  //   C
endmodule
